# Fritzing sketch MicroPython Rover wiring diagram (saved by Fritzing 0.9.3b)

parts:
  M2 = DC Motor
  Part4 = Bluetooth HC-05
  Part7 = BMP180 Breakout [part_number=SEN-11824]
  M3 = DC Motor
  PART2 = Motor Driver 1A Dual TB6612FNG [part_number=ROB_09457]
  Part9 = SparkFun 9 Degrees of Freedom Breakout - MPU-9150 [part_number=SEN-11486]
  U1 = LIPO-1000mAh [package=lipo-1000]
  Part10 = SRF04 Ultrasonic Rangefinder
  SERVO1 = Hitec HS-55 Servo [part_number=31055S]
  SERVO2 = Hitec HS-55 Servo [part_number=31055S]
  pyboard1 = Micro Python pyboard [part_number=PYBv10b]

nets:
  N1: M2.pin_1, PART2.A02
  N2: M2.pin_2, PART2.A01
  N3: Part4.RXD, pyboard1.X3
  N4: Part4.TXD, pyboard1.X4
  N5: Part4.GND, pyboard1.P9D_GND
  VCC: Part4.VCC, Part9.VCC, pyboard1.Y15_3V3
  N6: Part7.SCL, pyboard1.X9
  N7: Part7.SDA, pyboard1.X10
  N8: Part7.GND, pyboard1.P9C_GND
  N9: Part7.3.3V, Part7.IO, pyboard1.X15_3V3
  N10: M3.pin_1, PART2.B01
  N11: M3.pin_2, PART2.B02
  N12: PART2.PWMA, pyboard1.Y7
  N13: PART2.AIN2, pyboard1.Y5
  N14: PART2.AIN1, pyboard1.Y6
  N15: PART2.STBY, pyboard1.X17_USR
  N16: PART2.BIN1, pyboard1.X11
  N17: PART2.BIN2, pyboard1.X12
  N18: PART2.PWMB, pyboard1.Y8
  N19: PART2.VM, U1.+
  N20: PART2.VCC, pyboard1.X16_VIN
  N21: Part9.GND, pyboard1.Y14_GND
  N22: Part9.SDA, pyboard1.Y10
  N23: Part9.SCL, pyboard1.Y9
  N24: Part10.VCC, pyboard1.Y16_VIN
  N25: Part10.TRIG, Part10.MODE, pyboard1.Y3
  N26: Part10.ECHO, pyboard1.Y4
  N27: Part10.GND, pyboard1.X14_GND
  N28: SERVO1.Signal, pyboard1.X1
  N29: SERVO1.Power, pyboard1.P10A_VIN
  N30: SERVO1.Ground, pyboard1.P9A_GND
  N31: SERVO2.Signal, pyboard1.X2
  N32: SERVO2.Power, pyboard1.P10B_VIN
  N33: SERVO2.Ground, pyboard1.P9B_GND

custom parts:
  BMP180 Breakout: This is a breadboard friendly breakout board for the BMP180 high-precision, temp and pressure sensor.
  Motor Driver 1A Dual TB6612FNG: The TB6612FNG motor driver can control up to two DC motors at a constant current of 1.2A (3.2A peak). Two input signals (IN1 and IN2) can be used to control the motor in one of four function modes - CW, CCW, short-brake, and stop. The two motor outputs (A and B) can be separately controlled, the speed of each motor is controlled via a PWM input signal with a frequency up to 100kHz. The STBY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
  SparkFun 9 Degrees of Freedom Breakout - MPU-9150: The SparkFun 9DOF MPU-9150 is the world’s first 9-axis MotionTracking MEMS device designed for the low power, low cost, and high performance requirements of consumer electronics equipment including smartphones, tablets and wearable sensors. And guess what? You get to play with it. This breakout board makes it easy to prototype with the InvenSense MPU-9150 by breaking out all the pins you need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
  LIPO-1000mAh: 1000mAh Lipo-battery
  SRF04 Ultrasonic Rangefinder: http://www.robot-electronics.co.uk/htm/srf04tech.htm https://www.dfrobot.com/wiki/index.php?title=SRF05_Ultrasonic_sensor_(SKU:SEN0006)
  Hitec HS-55 Servo: HS-55 Economy Feather Servo Product Description The HS-55 set the standard for affordable performance, offering precision components that have been engineered to provide long lasting trouble free service! Featured in a hundred model aircraft reviews worldwide, the HS-55 is your best choice when it comes to controlling ”smaller” Electric’s and Park Flyers. Features Affordable Performance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
